// Logisim project 22810211 Led7Doan.circ as structural Verilog: 1 circuit, main circuit main
module main (
  input  I3,
  input  i2,
  input  i1,
  input  i0
);

  wire i1_ni0_out, i1i0_out, i2_ni0_out, i2_ni1_out, i2_ni1i0_out, i2i0_out, ni1_ni0_out, ni2_ni0_out,
       ni2i1_out, not_1_out, not_2_out, not_3_out, not_4_out, or_1_out, or_2_out, or_3_out, or_4_out,
       or_5_out, or_6_out, or_7_out;

  not not_1 (not_1_out, I3);
  not not_2 (not_2_out, i2);
  not not_3 (not_3_out, i1);
  not not_4 (not_4_out, i0);
  and i2i0 (i2i0_out, i2, i0);
  and i1i0 (i1i0_out, i0, i1);
  and i2_ni0 (i2_ni0_out, i2, not_4_out);
  and ni1_ni0 (ni1_ni0_out, not_3_out, not_4_out);
  and i2_ni1 (i2_ni1_out, i2, not_3_out);
  and ni2_ni0 (ni2_ni0_out, not_2_out, not_4_out);
  and ni2i1 (ni2i1_out, not_2_out, i1);
  and i1_ni0 (i1_ni0_out, not_4_out, i1);
  and i2_ni1i0 (i2_ni1i0_out, not_3_out, i0, i2);
  or or_1 (or_1_out, not_3_out, i2, i0);
  or or_2 (or_2_out, i1i0_out, not_2_out, ni1_ni0_out);
  or or_3 (or_3_out, I3, i2_ni1_out, i1_ni0_out, ni2i1_out);
  or or_4 (or_4_out, i1_ni0_out, ni2_ni0_out);
  or or_5 (or_5_out, ni1_ni0_out, i2_ni0_out, I3, i2_ni1_out);
  or or_6 (or_6_out, ni2_ni0_out, ni2i1_out, i1_ni0_out, i2_ni1i0_out, I3);
  or or_7 (or_7_out, i1, i2i0_out, I3, ni2_ni0_out);
  _7_Segment_Display u_7_segment_display_1 (
    .g(or_3_out), .f(or_5_out), .a(or_7_out), .b(or_2_out), .e(or_4_out), .d(or_6_out), .c(or_1_out));  // open: dp

  // Notes on the sheet:
  //   D3
  //   D5
  //   D0
  //   D1
  //   D2
  //   D4
endmodule
